# Fritzing sketch unity-controller-firmware (saved by Fritzing 0.9.3b)
breadboards: 1

parts:
  VCC1 = 4 x AAA Battery Mount [part_number=https://www.adafruit.com/product/830]
  Part1 = Photon
  Part2 = Adafruit MMA8451 Accelerometer [part_number=https://www.adafruit.com/product/2019]
  Part3 = Adafruit DRV2605L [part_number=https://www.adafruit.com/product/2305]
  MOTOR1 = Vibration Motor [part_number=https://www.adafruit.com/product/1201]
  U1 = TMP36 [part_number=https://www.adafruit.com/product/165 package=to-92]
  R1 = Photocell (LDR) [part_number=https://www.adafruit.com/product/161 package=THT]
  R2 = Resistor [tolerance=±5% resistance=10k package=THT]
  J1 = Piezo Speaker [part_number=https://www.adafruit.com/product/160]
  LED2 = RGB LED (com. cathode, rbg) [part_number=https://www.adafruit.com/product/1938 package="5 mm [THT]"]
  PIR1 = PIR sensor

nets:
  GND: VCC1.-, Part1.GND, Part2.GND, Part3.GND, U1.GND, R2.Pin_1, J1.pin2, LED2.GND, PIR1.GND
  VIN: VCC1.+, Part1.VIN, PIR1.VDD
  N1: Part1.A0, U1.VOUT
  N2: Part1.A1, R1.pin_0, R2.Pin_0
  N3: Part1.D0, Part2.SDA, Part3.SDA
  N4: Part1.D1, Part2.SCL, Part3.SCL
  N5: Part1.D2, PIR1.SIG
  N6: Part1.D3, J1.pin1
  N7: Part1.D6, LED2.DATA_IN
  3V3: Part1.3V3, Part2.+3V3, Part3.VIN, U1.VCC, R1.pin_1, LED2.+5
  N8: Part3.OUT+, MOTOR1.NEG
  N9: Part3.OUT-, MOTOR1.POS

notes:
  +3.3V
  GND
  5mm Neopixel Pinout
  1: Data IN [LEFT] (short)
  2: +V (short)
  3: GND (long)
  4: Data OUT [RIGHT] (long)
  +6V

custom parts:
  Adafruit MMA8451 Accelerometer: So many accelerometers and so little time! We've expanded our accelerometer selection even more with this high-precision and inexpensive MMA8451 Triple-Axis Accelerometer w/ 14-bit ADC. You can detect motion, tilt and basic orientation with a digital accelerometer - and the MMA8451 is a great accelerometer to start with. It has a wide usage range, from +-2g up to +-8g yet is easy to use with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
  Adafruit DRV2605L: The DRV2605 from TI is a fancy little motor driver. Rather than controlling a stepper motor or DC motor, its designed specifically for controlling haptic motors - buzzers and vibration motors. Normally one would just turn those kinds of motors on and off, but this driver has the ability to have various effects when driving a vibe motor. For example, ramping the vibration level up and down,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
  Vibration Motor: An eccentric vibration motor!
  RGB LED (com. cathode, rbg): A 5mm tri-color LED with red, green and blue inside. Pin order: red - com. cathode - blue - green
